# Fritzing sketch DiagramaCasa (saved by Fritzing 0.9.3b)
breadboards: 1

parts:
  Componente1 = Arduino Mega 2560 (Rev3)
  KY-1 = Keyes Relay [package=THT]
  LED1 = RGB LED - (4 legs) [package="5 mm [THT]"]
  LED2 = RGB LED - (4 legs) [package="5 mm [THT]"]
  LED3 = RGB LED - (4 legs) [package="5 mm [THT]"]
  LED4 = RGB LED - (4 legs) [package="5 mm [THT]"]
  LED5 = RGB LED - (4 legs) [package="5 mm [THT]"]
  LED6 = RGB LED - (4 legs) [package="5 mm [THT]"]
  LED7 = RGB LED - (4 legs) [package="5 mm [THT]"]
  LED8 = RGB LED - (4 legs) [package="5 mm [THT]"]
  LED9 = RGB LED - (4 legs) [package="5 mm [THT]"]
  LED10 = RGB LED - (4 legs) [package="5 mm [THT]"]
  LED11 = RGB LED - (4 legs) [package="5 mm [THT]"]
  LED12 = RGB LED - (4 legs) [package="5 mm [THT]"]
  KY-2 = Keyes Relay [package=THT]
  KY-3 = Keyes Relay [package=THT]
  KY-4 = Keyes Relay [package=THT]
  KY-5 = Keyes Relay [package=THT]
  KY-6 = Keyes Relay [package=THT]
  KY-7 = Keyes Relay [package=THT]
  KY-8 = Keyes Relay [package=THT]
  KY-9 = Keyes Relay [package=THT]
  KY-10 = Keyes Relay [package=THT]
  KY-11 = Keyes Relay [package=THT]
  KY-12 = Keyes Relay [package=THT]

nets:
  N1: Componente1.D21/SCL, Componente1.SCL, LED7.red_cathode, KY-7.NC
  N2: Componente1.D20/SDA, KY-7.signal
  N3: Componente1.D19/RX1, LED6.green_cathode
  N4: Componente1.D18/TX1, LED6.red_cathode
  N5: Componente1.D17_PWM/RX2, KY-6.signal
  N6: Componente1.D16_PWM/TX2, LED5.green_cathode
  N7: Componente1.D15/RX3, LED5.red_cathode
  N8: Componente1.D14/TX3, KY-5.signal
  N9: Componente1.D13_PWM, LED4.green_cathode
  N10: Componente1.D12_PWM, LED4.red_cathode
  N11: Componente1.D11_PWM, KY-4.signal
  N12: Componente1.D10_PWM, LED3.green_cathode
  N13: Componente1.D9_PWM, LED3.red_cathode
  N14: Componente1.D8_PWM, KY-3.signal
  N15: Componente1.D2_PWM, KY-1.signal
  N16: Componente1.D3_PWM, LED1.red_cathode
  N17: Componente1.D4_PWM, LED1.green_cathode
  N18: Componente1.D5_PWM, KY-2.signal
  N19: Componente1.D6_PWM, LED2.red_cathode
  N20: Componente1.D7_PWM, LED2.green_cathode
  N21: Componente1.D22, LED7.green_cathode
  N22: Componente1.D23, KY-8.signal
  N23: Componente1.D24, LED8.red_cathode
  N24: Componente1.D25, LED8.green_cathode
  N25: Componente1.D26, KY-9.signal
  N26: Componente1.D27, LED9.red_cathode
  N27: Componente1.D28, LED9.green_cathode
  N28: Componente1.D29, KY-10.signal
  N29: Componente1.D30, LED10.red_cathode
  N30: Componente1.D31, LED10.green_cathode
  N31: Componente1.D32, KY-11.signal
  N32: Componente1.D33, LED11.red_cathode
  N33: Componente1.D34, LED11.green_cathode
  N34: Componente1.D35, KY-12.signal
  N35: Componente1.D36, LED12.red_cathode
  N36: Componente1.D37, LED12.green_cathode
  N37: KY-1.power, LED3.common_anode, KY-2.power, KY-3.power, KY-4.power, KY-5.power, KY-6.power, KY-7.power, KY-8.power, KY-9.power, KY-10.power, KY-11.power, KY-12.power
  N38: KY-1.ground, LED1.common_anode, LED2.common_anode, LED4.common_anode, LED5.common_anode, LED6.common_anode, LED7.common_anode, LED8.common_anode, LED9.common_anode, LED10.common_anode, LED11.common_anode, LED12.common_anode, KY-2.ground, KY-3.ground, KY-4.ground, KY-5.ground, KY-6.ground, KY-7.ground, KY-8.ground, KY-9.ground, KY-10.ground, KY-11.ground

custom parts:
  Keyes Relay: The Keyes 5V relay module is suitable for SCM development, home appliance control. It uses a 5V~12V TIL control signal which can control DC / AC signal.
